// Logisim project cpu.circ as structural Verilog
module fetch (
);

  instruction_memory instruction_memory_1 ();  // open: PC, clk, byte_0, byte_1, byte_2, byte_3, byte_4, byte_5, byte_6, byte_7, byte_8, byte_9
endmodule

module instruction_memory (
  input  [63:0] PC,
  input  clk,
  output [7:0] byte_0,
  output [7:0] byte_1,
  output [7:0] byte_2,
  output [7:0] byte_3,
  output [7:0] byte_4,
  output [7:0] byte_5,
  output [7:0] byte_6,
  output [7:0] byte_7,
  output [7:0] byte_8,
  output [7:0] byte_9
);

  wire and_13_out, and_14_out, and_15_out, and_16_out, and_17_out, and_18_out, and_19_out, and_20_out,
       and_21_out, d_ff_1_q, d_ff_1_qn, decoder_1_out0, decoder_1_out1, decoder_1_out2, decoder_1_out3,
       decoder_1_out4, decoder_1_out5, decoder_1_out6, decoder_1_out7, decoder_1_out8, decoder_1_out9,
       or_1_out, or_4_out, or_5_out;
  wire [3:0] adder_2_out, and_1_out, and_2_out, and_3_out, and_4_out, and_5_out, and_6_out, and_7_out,
       and_8_out, and_9_out, and_10_out, and_11_out, and_12_out, or_2_out, or_3_out, register_1_q;
  wire [7:0] ram_1_dout;
  wire [11:0] adder_1_out;

  D_Flip_Flop d_ff_1 (.D(or_1_out), .clk(clk), .Q(d_ff_1_q), .Qn(d_ff_1_qn));  // open: preset, reset
  or or_1 (or_1_out, d_ff_1_q, d_ff_1_qn);
  Register #(.width(4)) register_1 (.D(adder_2_out), .en(d_ff_1_q), .clk(clk), .Q(register_1_q));  // open: clr
  RAM #(.addrWidth(12)) ram_1 (.addr(adder_1_out), .oe(clk), .clk(clk), .dout(ram_1_dout));  // open: we, din
  Adder #(.width(12)) adder_1 (.a(PC[11:0]), .b({{8{1'b0}}, register_1_q}), .out(adder_1_out));  // open: cin, cout
  Adder #(.width(4)) adder_2 (.a(register_1_q), .b(4'b0001), .out(adder_2_out));  // open: cin, cout
  assign and_1_out = byte_0[7:4] & 4'b0010;  // AND_Gate and_1, 4 bits wide
  assign and_2_out = byte_0[7:4] & 4'b0011;  // AND_Gate and_2, 4 bits wide
  assign and_3_out = byte_0[7:4] & 4'b0100;  // AND_Gate and_3, 4 bits wide
  assign and_4_out = byte_0[7:4] & 4'b0101;  // AND_Gate and_4, 4 bits wide
  assign and_5_out = byte_0[7:4] & 4'b0110;  // AND_Gate and_5, 4 bits wide
  assign and_6_out = byte_0[7:4] & 4'b1010;  // AND_Gate and_6, 4 bits wide
  assign and_7_out = byte_0[7:4] & 4'b1011;  // AND_Gate and_7, 4 bits wide
  assign and_8_out = byte_0[7:4] & 4'b0011;  // AND_Gate and_8, 4 bits wide
  assign and_9_out = byte_0[7:4] & 4'b0100;  // AND_Gate and_9, 4 bits wide
  assign and_10_out = byte_0[7:4] & 4'b0101;  // AND_Gate and_10, 4 bits wide
  assign and_11_out = byte_0[7:4] & 4'b0111;  // AND_Gate and_11, 4 bits wide
  assign and_12_out = byte_0[7:4] & 4'b1000;  // AND_Gate and_12, 4 bits wide
  assign or_2_out = and_1_out | and_2_out | and_3_out | and_4_out | and_5_out | and_6_out | and_7_out;  // OR_Gate or_2, 4 bits wide
  assign or_3_out = and_8_out | and_9_out | and_10_out | and_11_out | and_12_out;  // OR_Gate or_3, 4 bits wide
  or or_4 (or_4_out, or_2_out[0], or_2_out[1], or_2_out[2], or_2_out[3]);
  or or_5 (or_5_out, or_3_out[0], or_3_out[1], or_3_out[2], or_3_out[3]);
  Decoder #(.select(4)) decoder_1 (
    .out0(decoder_1_out0), .out1(decoder_1_out1), .out2(decoder_1_out2), .out3(decoder_1_out3),
    .out4(decoder_1_out4), .out5(decoder_1_out5), .out6(decoder_1_out6), .out7(decoder_1_out7),
    .out8(decoder_1_out8), .out9(decoder_1_out9), .sel(register_1_q));  // open: out10, out11, out12, out13, out14, out15, en
  assign byte_0 = decoder_1_out0 ? ram_1_dout : 8'bz;  // Controlled_Buffer controlled_buffer_1
  assign byte_1 = and_13_out ? ram_1_dout : 8'bz;  // Controlled_Buffer controlled_buffer_2
  and and_13 (and_13_out, or_4_out, decoder_1_out1);
  assign byte_2 = and_14_out ? ram_1_dout : 8'bz;  // Controlled_Buffer controlled_buffer_3
  and and_14 (and_14_out, or_5_out, decoder_1_out2);
  assign byte_3 = and_15_out ? ram_1_dout : 8'bz;  // Controlled_Buffer controlled_buffer_4
  and and_15 (and_15_out, or_5_out, decoder_1_out3);
  assign byte_4 = and_16_out ? ram_1_dout : 8'bz;  // Controlled_Buffer controlled_buffer_5
  and and_16 (and_16_out, or_5_out, decoder_1_out4);
  assign byte_5 = and_17_out ? ram_1_dout : 8'bz;  // Controlled_Buffer controlled_buffer_6
  and and_17 (and_17_out, or_5_out, decoder_1_out5);
  assign byte_6 = and_18_out ? ram_1_dout : 8'bz;  // Controlled_Buffer controlled_buffer_7
  and and_18 (and_18_out, or_5_out, decoder_1_out6);
  assign byte_7 = and_19_out ? ram_1_dout : 8'bz;  // Controlled_Buffer controlled_buffer_8
  and and_19 (and_19_out, or_5_out, decoder_1_out7);
  assign byte_8 = and_20_out ? ram_1_dout : 8'bz;  // Controlled_Buffer controlled_buffer_9
  and and_20 (and_20_out, or_5_out, decoder_1_out8);
  assign byte_9 = and_21_out ? ram_1_dout : 8'bz;  // Controlled_Buffer controlled_buffer_10
  and and_21 (and_21_out, or_5_out, decoder_1_out9);
endmodule
