// Logisim project execution.circ as structural Verilog: 8 circuits, main circuit execute_main
module execute_main (
  input  [3:0] icode,
  input  [3:0] ifun,
  input  [63:0] valA,
  input  [63:0] valC,
  input  [63:0] valB,
  output [63:0] out_6,
  output out_7
);

  wire setcc_1_setcc_output;
  wire [1:0] alu_fun_1_alu_funcoutput;
  wire [2:0] alu_1_cc_input, cc_1_cc_output;
  wire [63:0] alu_a_1_alu_a_output, alu_b_1_alu_a_output;

  cond cond_1 (.ifun(ifun), .CC_output(cc_1_cc_output), .cnd(out_7));
  CC cc_1 (.ALU_output(alu_1_cc_input), .setCC(setcc_1_setcc_output), .CC_output(cc_1_cc_output));
  setCC setcc_1 (.icode(icode), .setCC_output(setcc_1_setcc_output));
  ALU alu_1 (
    .alu_a(alu_a_1_alu_a_output), .alu_b(alu_b_1_alu_a_output), .alu_func(alu_fun_1_alu_funcoutput),
    .CC_input(alu_1_cc_input), .valE(out_6));
  ALU_A alu_a_1 (.valA(valA), .valC(valC), .icode(icode), .ALU_A_Output(alu_a_1_alu_a_output));
  ALU_B alu_b_1 (.valB(valB), .icode(icode), .ALU_A_Output(alu_b_1_alu_a_output));
  ALU_fun alu_fun_1 (.ifun(ifun), .icode(icode), .alu_funcOutput(alu_fun_1_alu_funcoutput));
endmodule

module setCC (
  input  [3:0] icode,
  output setCC_output
);

  wire not_1_out, not_2_out;

  not not_1 (not_1_out, icode[0]);
  not not_2 (not_2_out, icode[3]);
  and and_1 (setCC_output, not_1_out, icode[1], icode[2], not_2_out);
endmodule

module ALU_A (
  input  [63:0] valA,
  input  [63:0] valC,
  input  [3:0] icode,
  output [63:0] ALU_A_Output
);

  wire [63:0] negator_1_out;

  Negator #(.width(64)) negator_1 (.in(64'h8), .out(negator_1_out));
  Multiplexer #(.select(4), .width(64)) multiplexer_1 (
    .in2(valA), .in3(valC), .in4(valC), .in5(valC), .in6(valA), .in10(negator_1_out), .in11(64'h8),
    .out(ALU_A_Output), .sel(icode));  // open: in0, in1, in7, in8, in9, in12, in13, in14, in15
endmodule

module ALU_B (
  input  [63:0] valB,
  input  [3:0] icode,
  output [63:0] ALU_A_Output
);

  Multiplexer #(.select(4), .width(64)) multiplexer_1 (
    .in2({64{1'b0}}), .in3({64{1'b0}}), .in4(valB), .in5(valB), .in6(valB), .in10(valB), .in11(valB),
    .out(ALU_A_Output), .sel(icode));  // open: in0, in1, in7, in8, in9, in12, in13, in14, in15
endmodule

module ALU_fun (
  input  [3:0] ifun,
  input  [3:0] icode,
  output [1:0] alu_funcOutput
);

  Multiplexer #(.select(4), .width(2)) multiplexer_1 (
    .in2(2'b00), .in3(2'b00), .in4(2'b00), .in5(2'b00), .in6(ifun[1:0]), .in7(2'b00), .in8(2'b00),
    .in9(2'b00), .in10(2'b00), .in11(2'b00), .out(alu_funcOutput), .sel(icode));  // open: in0, in1, in12, in13, in14, in15
endmodule

module CC (
  input  [2:0] ALU_output,
  input  setCC,
  output [2:0] CC_output
);

  wire clock_1_out;

  Register #(.width(3)) register_1 (.D(ALU_output), .en(setCC), .clk(clock_1_out), .Q(CC_output));  // open: clr
  Clock clock_1 (.out(clock_1_out));
endmodule

module cond (
  input  [3:0] ifun,
  input  [2:0] CC_output,
  output cnd
);

  wire and_1_out, and_2_out, and_3_out, ifun1_out, ifun2_out, ifun3_out, ifun4_out, ifun_0_out, ifun_5_out,
       ifun_6_out, not_1_out, not_2_out, not_3_out, not_4_out, not_5_out, not_6_out, not_7_out, not_8_out,
       not_9_out, not_10_out, not_11_out, not_12_out, not_13_out, not_14_out, not_15_out, not_16_out,
       not_17_out, not_18_out, not_19_out, not_20_out, not_21_out, not_22_out, not_23_out, or_1_out,
       SF_and_OF_out;

  and SF_and_OF (SF_and_OF_out, CC_output[0], CC_output[1]);
  not not_1 (not_1_out, ifun[0]);
  not not_2 (not_2_out, ifun[1]);
  and ifun_0 (ifun_0_out, not_1_out, not_2_out, not_3_out, not_4_out);
  not not_3 (not_3_out, ifun[2]);
  not not_4 (not_4_out, ifun[3]);
  not not_5 (not_5_out, ifun[1]);
  and ifun1 (ifun1_out, ifun[0], not_5_out, not_6_out, not_7_out);
  not not_6 (not_6_out, ifun[2]);
  not not_7 (not_7_out, ifun[3]);
  or or_1 (or_1_out, SF_and_OF_out, CC_output[2]);
  not not_8 (not_8_out, ifun[0]);
  and ifun2 (ifun2_out, SF_and_OF_out, not_8_out, ifun[1], not_9_out, not_10_out);
  not not_9 (not_9_out, ifun[2]);
  not not_10 (not_10_out, ifun[3]);
  and ifun3 (ifun3_out, CC_output[2], ifun[0], ifun[1], not_11_out, not_12_out);
  not not_11 (not_11_out, ifun[2]);
  not not_12 (not_12_out, ifun[3]);
  not not_13 (not_13_out, CC_output[2]);
  not not_14 (not_14_out, ifun[0]);
  not not_15 (not_15_out, ifun[1]);
  and ifun4 (ifun4_out, not_13_out, not_14_out, not_15_out, ifun[2], not_16_out);
  not not_16 (not_16_out, ifun[3]);
  not not_17 (not_17_out, SF_and_OF_out);
  not not_18 (not_18_out, ifun[1]);
  and ifun_5 (ifun_5_out, not_17_out, ifun[0], not_18_out, ifun[2], not_19_out);
  not not_19 (not_19_out, ifun[3]);
  not not_20 (not_20_out, ifun[0]);
  and ifun_6 (ifun_6_out, not_20_out, ifun[1], ifun[2], not_21_out);
  not not_21 (not_21_out, ifun[3]);
  not not_22 (not_22_out, SF_and_OF_out);
  and and_1 (and_1_out, not_22_out, not_23_out);
  not not_23 (not_23_out, CC_output[2]);
  and and_2 (and_2_out, ifun1_out, or_1_out);
  and and_3 (and_3_out, ifun_6_out, and_1_out);
  or or_2 (cnd, ifun_0_out, and_2_out, ifun2_out, ifun3_out, ifun4_out, ifun_5_out, and_3_out);
endmodule

module ALU (
  input  [63:0] alu_a,
  input  [63:0] alu_b,
  input  [1:0] alu_func,
  output [2:0] CC_input,
  output [63:0] valE
);

  wire adder_1_cout, adder_2_cout, and_2_out, and_3_out, and_4_out, and_5_out, not_1_out, not_2_out,
       not_3_out;
  wire [63:0] adder_1_out, adder_2_out, and_1_out, negator_1_out, xor_1_out;

  assign and_1_out = alu_a & alu_b;  // AND_Gate and_1, 64 bits wide
  assign xor_1_out = alu_a ^ alu_b;  // XOR_Gate xor_1, 64 bits wide
  Negator #(.width(64)) negator_1 (.in(alu_b), .out(negator_1_out));
  and and_2 (and_2_out, alu_func[0], not_1_out);
  not not_1 (not_1_out, alu_func[1]);
  Adder #(.width(64)) adder_1 (.a(alu_a), .b(alu_b), .out(adder_1_out), .cout(adder_1_cout));  // open: cin
  Adder #(.width(64)) adder_2 (.a(alu_a), .b(negator_1_out), .out(adder_2_out), .cout(adder_2_cout));  // open: cin
  and and_3 (and_3_out, adder_2_cout, and_2_out);
  not not_2 (not_2_out, alu_func[0]);
  and and_4 (and_4_out, not_2_out, not_3_out);
  not not_3 (not_3_out, alu_func[1]);
  and and_5 (and_5_out, and_4_out, adder_1_cout);
  Multiplexer #(.select(2), .width(64)) multiplexer_1 (
    .in0(adder_1_out), .in1(adder_2_out), .in2(and_1_out), .in3(xor_1_out), .out(valE), .sel(alu_func));
  or or_1 (CC_input[0], and_5_out, and_3_out);
  Comparator #(.width(64)) comparator_1 (.a(valE), .b({64{1'b0}}), .eq(CC_input[2]), .lt(CC_input[1]));  // open: gt
endmodule
