// Logisim project pc_update.circ as structural Verilog: 2 circuits, main circuit pc_update
module pc_update (
  input  in_1,
  input  [63:0] in_2,
  input  [63:0] in_3,
  input  [3:0] in_4,
  input  [63:0] in_5,
  output [63:0] PC
);

  newPC newpc_1 (.cnd(in_1), .valC(in_2), .valM(in_3), .icode(in_4), .valP(in_5), .PC(PC));
endmodule

module newPC (
  input  cnd,
  input  [63:0] valC,
  input  [63:0] valM,
  input  [3:0] icode,
  input  [63:0] valP,
  output [63:0] PC
);

  wire [63:0] multiplexer_1_out;

  Multiplexer #(.width(64)) multiplexer_1 (.in0(valP), .in1(valC), .out(multiplexer_1_out), .sel(cnd));
  Multiplexer #(.select(4), .width(64)) multiplexer_2 (
    .in0({64{1'b0}}), .in1(valC), .in2(valC), .in3(valC), .in4(valC), .in5(valC), .in6(valC),
    .in7(multiplexer_1_out), .in10(valC), .in11(valC), .out(PC), .sel(icode));  // open: in8, in9, in12, in13, in14, in15
endmodule
