// Logisim project rita_fetch.circ as structural Verilog: 7 circuits, main circuit fetch_stage
module fetch_stage (
  input  [11:0] PC
);

  wire [7:0] instruction_memory_1_byte0;

  split split_1 (.Byte0(instruction_memory_1_byte0));  // open: icode, ifun
  instruction_memory instruction_memory_1 (
    .PC(PC), .Byte0(instruction_memory_1_byte0));  // open: Byte1, Byte2, Byte3, Byte4, Byte5, Byte6, Byte7, Byte8, Byte9
  align align_1 ();  // open: Byte1, Byte2, rA, Byte3, Byte4, Byte5, rB, Byte6, Byte7, valC, Byte8, Byte9, needRegIDs
endmodule

module instruction_memory (
  input  [11:0] PC,
  output [7:0] Byte0,
  output [7:0] Byte1,
  output [7:0] Byte2,
  output [7:0] Byte3,
  output [7:0] Byte4,
  output [7:0] Byte5,
  output [7:0] Byte6,
  output [7:0] Byte7,
  output [7:0] Byte8,
  output [7:0] Byte9
);

  wire clock_1_out;

  Clock clock_1 (.out(clock_1_out));
  RAM #(.addrWidth(12)) ram_1 (.addr(PC), .clk(clock_1_out));  // open: we, oe, din, dout
endmodule

module split (
  input  [7:0] Byte0,
  output [3:0] icode,
  output [3:0] ifun
);


  assign icode = Byte0[3:0];
  assign ifun = Byte0[7:4];
endmodule

module align (
  output Byte1,
  output Byte2,
  output [1:0] rA,
  output Byte3,
  output Byte4,
  output Byte5,
  output [1:0] rB,
  output Byte6,
  output Byte7,
  output [1:0] valC,
  output Byte8,
  output Byte9,
  output needRegIDs
);
endmodule

module pc_increment (
  input  needValC,
  input  needRegIDs,
  input  [11:0] PC,
  output [11:0] valP
);

  wire [7:0] bit_extender_1_out, bit_extender_2_out, multiplier_1_out;
  wire [11:0] bit_extender_3_out;

  assign bit_extender_1_out = {{4{1'b1}}, 4'b1000};  // Bit_Extender bit_extender_1
  assign bit_extender_2_out = {{7{needValC}}, needValC};  // Bit_Extender bit_extender_2
  Multiplier multiplier_1 (
    .a(bit_extender_1_out), .b(bit_extender_2_out), .out(multiplier_1_out), .cin(8'h1));  // open: cout
  Adder #(.width(12)) adder_1 (.a(bit_extender_3_out), .b(PC), .out(valP), .cin(needRegIDs));  // open: cout
  assign bit_extender_3_out = {{4{multiplier_1_out[7]}}, multiplier_1_out};  // Bit_Extender bit_extender_3
endmodule

module need_valC (
  input  [3:0] icode,
  output needValC
);

  wire and_1_out, and_2_out, and_3_out, and_4_out, not_1_out, not_2_out, not_3_out, not_4_out, not_5_out;

  not not_1 (not_1_out, icode[3]);
  not not_2 (not_2_out, icode[2]);
  and and_1 (and_1_out, not_1_out, not_2_out, icode[1], icode[0]);
  and and_2 (and_2_out, not_1_out, icode[2], not_3_out, not_4_out);
  not not_3 (not_3_out, icode[1]);
  not not_4 (not_4_out, icode[0]);
  and and_3 (and_3_out, not_1_out, icode[2], not_5_out, icode[0]);
  not not_5 (not_5_out, icode[1]);
  and and_4 (and_4_out, not_1_out, icode[2], icode[1], icode[0]);
  or or_1 (needValC, and_1_out, and_2_out, and_3_out, and_4_out);
endmodule

module need_regIDs (
  input  [3:0] icode,
  output needRegIDsFlag
);

  wire and_1_out, and_2_out, and_3_out, and_4_out, and_5_out, and_6_out, and_7_out, not_1_out, not_2_out,
       not_3_out, not_4_out;

  not not_1 (not_1_out, icode[3]);
  not not_2 (not_2_out, icode[2]);
  not not_3 (not_3_out, icode[0]);
  not not_4 (not_4_out, icode[1]);
  and and_1 (and_1_out, not_3_out, icode[1], not_2_out, not_1_out);
  and and_2 (and_2_out, icode[0], icode[1], not_2_out, not_1_out);
  and and_3 (and_3_out, not_3_out, not_4_out, icode[2], not_1_out);
  and and_4 (and_4_out, icode[0], not_4_out, icode[2], not_1_out);
  and and_5 (and_5_out, icode[0], not_4_out, icode[2], not_1_out);
  and and_6 (and_6_out, not_3_out, icode[0], not_2_out, icode[3]);
  and and_7 (and_7_out, icode[0], icode[1], not_2_out, icode[3]);
  or or_1 (needRegIDsFlag, and_1_out, and_2_out, and_3_out, and_4_out, and_5_out, and_6_out, and_7_out);
endmodule
