// Logisim project rita_fetch2.circ as structural Verilog: 8 circuits, main circuit fetch_stage
module fetch_stage (
  input  [11:0] PC
);

  wire [7:0] instruction_memory_1_byte0;

  split split_1 (.Byte0(instruction_memory_1_byte0));  // open: icode, ifun
  instruction_memory instruction_memory_1 (
    .PC(PC), .Byte0(instruction_memory_1_byte0));  // open: Byte1, Byte2, Byte3, Byte4, Byte5, Byte6, Byte7, Byte8, Byte9
  align align_1 ();  // open: Byte1, Byte2, Byte3, Byte4, Byte5, Byte6, Byte7, Byte8, Byte9, NeedRegIDs, rA, rB, valC
endmodule

module instruction_memory (
  input  [11:0] PC,
  output [7:0] Byte0,
  output [7:0] Byte1,
  output [7:0] Byte2,
  output [7:0] Byte3,
  output [7:0] Byte4,
  output [7:0] Byte5,
  output [7:0] Byte6,
  output [7:0] Byte7,
  output [7:0] Byte8,
  output [7:0] Byte9
);

  wire clock_1_out;

  Clock clock_1 (.out(clock_1_out));
  RAM #(.addrWidth(12)) ram_1 (.addr(PC), .clk(clock_1_out));  // open: we, oe, din, dout
endmodule

module split (
  input  [7:0] Byte0,
  output [3:0] icode,
  output [3:0] ifun
);


  assign icode = Byte0[3:0];
  assign ifun = Byte0[7:4];
endmodule

module align (
  input  [7:0] Byte1,
  input  [7:0] Byte2,
  input  [7:0] Byte3,
  input  [7:0] Byte4,
  input  [7:0] Byte5,
  input  [7:0] Byte6,
  input  [7:0] Byte7,
  input  [7:0] Byte8,
  input  [7:0] Byte9,
  input  NeedRegIDs,
  output [3:0] rA,
  output [3:0] rB,
  output [63:0] valC
);

  wire clock_1_out, clock_2_out, clock_3_out;

  Register #(.width(4)) register_1 (.D(Byte1[7:4]), .en(NeedRegIDs), .clk(clock_1_out), .Q(rA));  // open: clr
  Clock clock_1 (.out(clock_1_out));
  Register #(.width(4)) register_2 (.D(Byte1[3:0]), .en(NeedRegIDs), .clk(clock_2_out), .Q(rB));  // open: clr
  Clock clock_2 (.out(clock_2_out));
  Register #(.width(64)) register_3 (.clk(clock_3_out), .Q(valC));  // open: D, en, clr
  Clock clock_3 (.out(clock_3_out));
endmodule

module pc_increment (
  input  needValC,
  input  needRegIDs,
  input  [11:0] PC,
  output [11:0] valP
);

  wire [7:0] bit_extender_1_out, bit_extender_2_out, multiplier_1_out;
  wire [11:0] bit_extender_3_out;

  assign bit_extender_1_out = {{4{1'b1}}, 4'b1000};  // Bit_Extender bit_extender_1
  assign bit_extender_2_out = {{7{needValC}}, needValC};  // Bit_Extender bit_extender_2
  Multiplier multiplier_1 (
    .a(bit_extender_1_out), .b(bit_extender_2_out), .out(multiplier_1_out), .cin(8'h1));  // open: cout
  Adder #(.width(12)) adder_1 (.a(bit_extender_3_out), .b(PC), .out(valP), .cin(needRegIDs));  // open: cout
  assign bit_extender_3_out = {{4{multiplier_1_out[7]}}, multiplier_1_out};  // Bit_Extender bit_extender_3
endmodule

module need_valC (
  input  [3:0] icode,
  output needValC
);

  wire and_1_out, and_2_out, and_3_out, and_4_out, not_1_out, not_2_out, not_3_out, not_4_out, not_5_out;

  not not_1 (not_1_out, icode[3]);
  not not_2 (not_2_out, icode[2]);
  and and_1 (and_1_out, not_1_out, not_2_out, icode[1], icode[0]);
  and and_2 (and_2_out, not_1_out, icode[2], not_3_out, not_4_out);
  not not_3 (not_3_out, icode[1]);
  not not_4 (not_4_out, icode[0]);
  and and_3 (and_3_out, not_1_out, icode[2], not_5_out, icode[0]);
  not not_5 (not_5_out, icode[1]);
  and and_4 (and_4_out, not_1_out, icode[2], icode[1], icode[0]);
  or or_1 (needValC, and_1_out, and_2_out, and_3_out, and_4_out);
endmodule

module need_regIDs (
  input  [3:0] icode,
  output needRegIDsFlag
);

  wire and_1_out, and_2_out, and_3_out, and_4_out, and_5_out, and_6_out, and_7_out, not_1_out, not_2_out,
       not_3_out, not_4_out;

  not not_1 (not_1_out, icode[3]);
  not not_2 (not_2_out, icode[2]);
  not not_3 (not_3_out, icode[0]);
  not not_4 (not_4_out, icode[1]);
  and and_1 (and_1_out, not_3_out, icode[1], not_2_out, not_1_out);
  and and_2 (and_2_out, icode[0], icode[1], not_2_out, not_1_out);
  and and_3 (and_3_out, not_3_out, not_4_out, icode[2], not_1_out);
  and and_4 (and_4_out, icode[0], not_4_out, icode[2], not_1_out);
  and and_5 (and_5_out, icode[0], not_4_out, icode[2], not_1_out);
  and and_6 (and_6_out, not_3_out, icode[0], not_2_out, icode[3]);
  and and_7 (and_7_out, icode[0], icode[1], not_2_out, icode[3]);
  or or_1 (needRegIDsFlag, and_1_out, and_2_out, and_3_out, and_4_out, and_5_out, and_6_out, and_7_out);
endmodule

module align_2 (
  input  [7:0] Byte1,
  input  [7:0] Byte2,
  input  [7:0] Byte3,
  input  [7:0] Byte4,
  input  [7:0] Byte5,
  input  [7:0] Byte6,
  input  [7:0] Byte7,
  input  [7:0] Byte8,
  input  [7:0] Byte9,
  input  NeedRegIDs,
  input  NeedValC,
  output [3:0] rA,
  output [3:0] rB,
  output [63:0] valC
);

  wire and_1_out, and_2_out, clock_1_out, clock_2_out, clock_3_out, clock_4_out, not_1_out;
  wire [63:0] register_3_q, register_4_q;

  and and_1 (and_1_out, NeedValC, not_1_out);
  not not_1 (not_1_out, NeedRegIDs);
  and and_2 (and_2_out, NeedValC, NeedRegIDs);
  Register #(.width(4)) register_1 (.D(Byte1[7:4]), .en(NeedRegIDs), .clk(clock_1_out), .Q(rA));  // open: clr
  Clock clock_1 (.out(clock_1_out));
  Register #(.width(4)) register_2 (.D(Byte1[3:0]), .en(NeedRegIDs), .clk(clock_2_out), .Q(rB));  // open: clr
  Clock clock_2 (.out(clock_2_out));
  Register #(.width(64)) register_3 (.en(and_1_out), .clk(clock_3_out), .Q(register_3_q));  // open: D, clr
  Clock clock_3 (.out(clock_3_out));
  Register #(.width(64)) register_4 (.en(and_2_out), .clk(clock_4_out), .Q(register_4_q));  // open: D, clr
  Clock clock_4 (.out(clock_4_out));
  assign valC = register_3_q | register_4_q;  // OR_Gate or_1, 64 bits wide
endmodule
