// Logisim project cpu.circ as structural Verilog: 6 circuits, main circuit main
module main (
);

  wire and_1_out, and_2_out, clock_1_out, comparator_1_eq, comparator_2_eq, comparator_3_eq,
       execute_main_1_cnd, fetch_1_regs_loaded, not_1_out;
  wire [3:0] fetch_1_icode, fetch_1_ifun, fetch_1_ra, fetch_1_rb;
  wire [11:0] fetch_1_curr_pc;
  wire [63:0] decode_and_write_back_1_vala, decode_and_write_back_1_valb, execute_main_1_vale, fetch_1_valc,
       fetch_1_valp, memory_1_vam, pc_update_1_pc;

  Clock clock_1 (.out(clock_1_out));
  and and_1 (and_1_out, not_1_out, clock_1_out);
  Comparator #(.mode("unsigned"), .width(12)) comparator_1 (
    .a(fetch_1_curr_pc), .b({12{1'b0}}), .eq(comparator_1_eq));  // open: gt, lt
  fetch fetch_1 (
    .PC(pc_update_1_pc), .clk(and_1_out), .icode(fetch_1_icode), .ifun(fetch_1_ifun), .rA(fetch_1_ra),
    .rB(fetch_1_rb), .valC(fetch_1_valc), .valP(fetch_1_valp), .regs_loaded(fetch_1_regs_loaded),
    .curr_pc(fetch_1_curr_pc));
  Comparator #(.mode("unsigned"), .width(4)) comparator_2 (
    .a(4'b0000), .b(fetch_1_icode), .eq(comparator_2_eq));  // open: gt, lt
  Comparator #(.mode("unsigned"), .width(4)) comparator_3 (
    .a(4'b0000), .b(fetch_1_ifun), .eq(comparator_3_eq));  // open: gt, lt
  not not_1 (not_1_out, and_2_out);
  and and_2 (and_2_out, comparator_2_eq, ~comparator_1_eq, comparator_3_eq);  // AND_Gate
  decode_and_write_back decode_and_write_back_1 (
    .Cnd(execute_main_1_cnd), .icode(fetch_1_icode), .rA(fetch_1_ra), .rB(fetch_1_rb),
    .valE(execute_main_1_vale), .valM(memory_1_vam), .clk(and_1_out), .in_8(fetch_1_regs_loaded),
    .valA(decode_and_write_back_1_vala), .valB(decode_and_write_back_1_valb));
  memory memory_1 (
    .icode(fetch_1_icode), .valE(execute_main_1_vale), .valA(decode_and_write_back_1_vala), .clk(and_1_out),
    .vaM(memory_1_vam));
  execute_main execute_main_1 (
    .icode(fetch_1_icode), .ifun(fetch_1_ifun), .valA(decode_and_write_back_1_vala),
    .valB(decode_and_write_back_1_valb), .valC(fetch_1_valc), .clk(and_1_out), .valE(execute_main_1_vale),
    .cnd(execute_main_1_cnd));
  pc_update pc_update_1 (
    .cnd(execute_main_1_cnd), .valC(fetch_1_valc), .valM(memory_1_vam), .icode(fetch_1_icode),
    .valP(fetch_1_valp), .PC(pc_update_1_pc));
endmodule

module fetch (
  input  [63:0] PC,
  input  clk,
  output [3:0] icode,
  output [3:0] ifun,
  output [3:0] rA,
  output [3:0] rB,
  output [63:0] valC,
  output [63:0] valP,
  output regs_loaded,
  output [11:0] curr_pc
);

  wire and_1_out, instruction_memory_1_need_regids, instruction_memory_1_need_valc, not_1_out;
  wire [7:0] instruction_memory_1_byte_9;
  wire [63:0] adder_1_out, adder_2_out, bit_extender_1_out, bit_extender_2_out, bit_extender_3_out,
       instruction_memory_1_byte_1, multiplier_1_out;

  assign bit_extender_1_out = {{52{1'b0}}, curr_pc};  // Bit_Extender bit_extender_1
  instruction_memory instruction_memory_1 (
    .PC(PC), .clk(clk), .need_regids(instruction_memory_1_need_regids),
    .need_valC(instruction_memory_1_need_valc), .byte_0({icode, ifun}),
    .byte_1(instruction_memory_1_byte_1[7:0]), .byte_2(instruction_memory_1_byte_1[15:8]),
    .byte_3(instruction_memory_1_byte_1[23:16]), .byte_4(instruction_memory_1_byte_1[31:24]),
    .byte_5(instruction_memory_1_byte_1[39:32]), .byte_6(instruction_memory_1_byte_1[47:40]),
    .byte_7(instruction_memory_1_byte_1[55:48]), .byte_8(instruction_memory_1_byte_1[63:56]),
    .byte_9(instruction_memory_1_byte_9), .init_pc(curr_pc), .regs_loaded(regs_loaded));
  assign bit_extender_2_out = {{63{1'b0}}, instruction_memory_1_need_valc};  // Bit_Extender bit_extender_2
  Adder #(.width(64)) adder_1 (.a(bit_extender_1_out), .b(64'h1), .out(adder_1_out));  // open: cin, cout
  Multiplier #(.width(64)) multiplier_1 (.a(bit_extender_2_out), .b(64'h8), .out(multiplier_1_out));  // open: cin, cout
  assign bit_extender_3_out = {{63{1'b0}}, instruction_memory_1_need_regids};  // Bit_Extender bit_extender_3
  Adder #(.width(64)) adder_2 (.a(multiplier_1_out), .b(adder_1_out), .out(adder_2_out));  // open: cin, cout
  Multiplexer #(.width(4)) multiplexer_1 (
    .in0(4'b1111), .in1(instruction_memory_1_byte_1[7:4]), .out(rA), .sel(instruction_memory_1_need_regids));
  Multiplexer #(.width(4)) multiplexer_2 (
    .in0(4'b1111), .in1(instruction_memory_1_byte_1[3:0]), .out(rB), .sel(instruction_memory_1_need_regids));
  and and_1 (and_1_out, ~instruction_memory_1_need_regids, instruction_memory_1_need_valc);  // AND_Gate
  Adder #(.width(64)) adder_3 (.a(bit_extender_3_out), .b(adder_2_out), .out(valP));  // open: cin, cout
  not not_1 (not_1_out, and_1_out);
  Multiplexer #(.width(64)) multiplexer_3 (
    .in0(instruction_memory_1_byte_1),
    .in1({instruction_memory_1_byte_9, instruction_memory_1_byte_1[63:8]}), .out(valC), .sel(not_1_out));
endmodule

module instruction_memory (
  input  [63:0] PC,
  input  clk,
  output need_regids,
  output need_valC,
  output [7:0] byte_0,
  output [7:0] byte_1,
  output [7:0] byte_2,
  output [7:0] byte_3,
  output [7:0] byte_4,
  output [7:0] byte_5,
  output [7:0] byte_6,
  output [7:0] byte_7,
  output [7:0] byte_8,
  output [7:0] byte_9,
  output [11:0] init_pc,
  output regs_loaded
);

  wire and_1_out, and_2_out, and_3_out, and_4_out, and_5_out, and_6_out, and_7_out, and_8_out, and_9_out,
       and_10_out, and_11_out, and_12_out, comparator_1_eq, comparator_2_eq, comparator_3_eq,
       comparator_4_eq, comparator_5_eq, comparator_6_eq, comparator_7_eq, comparator_8_eq, comparator_9_eq,
       comparator_10_eq, comparator_11_eq, comparator_12_eq, comparator_13_eq, comparator_14_eq,
       comparator_15_eq, comparator_16_eq, decoder_1_out0, decoder_1_out1, decoder_1_out2, decoder_1_out3,
       decoder_1_out4, decoder_1_out5, decoder_1_out6, decoder_1_out7, decoder_1_out8, decoder_1_out9,
       or_1_out, or_2_out, or_5_out;
  wire [3:0] counter_1_q;
  wire [7:0] ram_1_dout;
  wire [11:0] adder_1_out, bit_extender_1_out;

  Register #(.width(12)) register_1 (.D(PC[11:0]), .en(or_1_out), .clk(clk), .Q(init_pc));  // open: clr
  or or_1 (or_1_out, and_1_out, comparator_3_eq);
  Counter #(.max('hf), .width(4)) counter_1 (
    .load(comparator_3_eq), .up(1'b1), .count(clk), .clk(clk), .D(4'b0000), .Q(counter_1_q));  // open: clr, carry
  assign bit_extender_1_out = {{8{1'b0}}, counter_1_q};  // Bit_Extender bit_extender_1
  Comparator #(.width(12)) comparator_1 (.a(init_pc), .b({12{1'b0}}), .eq(comparator_1_eq));  // open: gt, lt
  Comparator #(.width(12)) comparator_2 (.a(PC[11:0]), .b({12{1'b0}}), .eq(comparator_2_eq));  // open: gt, lt
  Comparator #(.width(4)) comparator_3 (.a(counter_1_q), .b(4'b1111), .eq(comparator_3_eq));  // open: gt, lt
  Comparator #(.width(4)) comparator_4 (.a(counter_1_q), .b(4'b0000), .eq(comparator_4_eq));  // open: gt, lt
  and and_1 (and_1_out, comparator_1_eq, comparator_2_eq);
  and and_2 (and_2_out, comparator_4_eq, or_2_out);
  RAM #(.addrWidth(12), .enables("line"), .\type ("nonvolatile")) ram_1 (
    .addr(adder_1_out), .clk(clk), .dout(ram_1_dout));  // open: we, din
  Adder #(.width(12)) adder_1 (.a(init_pc), .b(bit_extender_1_out), .out(adder_1_out));  // open: cin, cout
  and and_3 (and_3_out, comparator_4_eq, need_valC);
  or or_2 (or_2_out, need_valC, need_regids);
  Comparator #(.width(4)) comparator_5 (.a(byte_0[7:4]), .b(4'b0010), .eq(comparator_5_eq));  // open: gt, lt
  Comparator #(.width(4)) comparator_6 (.a(byte_0[7:4]), .b(4'b0011), .eq(comparator_6_eq));  // open: gt, lt
  Comparator #(.width(4)) comparator_7 (.a(byte_0[7:4]), .b(4'b0100), .eq(comparator_7_eq));  // open: gt, lt
  Comparator #(.width(4)) comparator_8 (.a(byte_0[7:4]), .b(4'b0101), .eq(comparator_8_eq));  // open: gt, lt
  Comparator #(.width(4)) comparator_9 (.a(byte_0[7:4]), .b(4'b0110), .eq(comparator_9_eq));  // open: gt, lt
  Comparator #(.width(4)) comparator_10 (.a(byte_0[7:4]), .b(4'b1010), .eq(comparator_10_eq));  // open: gt, lt
  Comparator #(.width(4)) comparator_11 (.a(byte_0[7:4]), .b(4'b1011), .eq(comparator_11_eq));  // open: gt, lt
  Comparator #(.width(4)) comparator_12 (.a(byte_0[7:4]), .b(4'b0011), .eq(comparator_12_eq));  // open: gt, lt
  Comparator #(.width(4)) comparator_13 (.a(byte_0[7:4]), .b(4'b0100), .eq(comparator_13_eq));  // open: gt, lt
  Comparator #(.width(4)) comparator_14 (.a(byte_0[7:4]), .b(4'b0101), .eq(comparator_14_eq));  // open: gt, lt
  Comparator #(.width(4)) comparator_15 (.a(byte_0[7:4]), .b(4'b0111), .eq(comparator_15_eq));  // open: gt, lt
  Comparator #(.width(4)) comparator_16 (.a(byte_0[7:4]), .b(4'b1000), .eq(comparator_16_eq));  // open: gt, lt
  or or_3 (need_valC, comparator_12_eq, comparator_13_eq, comparator_14_eq, comparator_15_eq, comparator_16_eq);
  or or_4 (need_regids, comparator_5_eq, comparator_6_eq, comparator_7_eq, comparator_8_eq, comparator_9_eq, comparator_10_eq, comparator_11_eq);
  Decoder #(.enable("false"), .select(4)) decoder_1 (
    .out0(decoder_1_out0), .out1(decoder_1_out1), .out2(decoder_1_out2), .out3(decoder_1_out3),
    .out4(decoder_1_out4), .out5(decoder_1_out5), .out6(decoder_1_out6), .out7(decoder_1_out7),
    .out8(decoder_1_out8), .out9(decoder_1_out9), .sel(counter_1_q));  // open: out10, out11, out12, out13, out14, out15
  or or_5 (or_5_out, need_valC, need_regids);
  Register register_2 (.D(ram_1_dout), .en(decoder_1_out0), .clk(clk), .Q(byte_0));  // open: clr
  Register register_3 (.D(ram_1_dout), .en(and_4_out), .clk(clk), .Q(byte_1), .clr(and_2_out));
  and and_4 (and_4_out, or_5_out, decoder_1_out1);
  Register register_4 (.D(ram_1_dout), .en(and_5_out), .clk(clk), .Q(byte_2), .clr(and_3_out));
  and and_5 (and_5_out, need_valC, decoder_1_out2);
  Register register_5 (.D(ram_1_dout), .en(and_6_out), .clk(clk), .Q(byte_3), .clr(and_3_out));
  and and_6 (and_6_out, need_valC, decoder_1_out3);
  Register register_6 (.D(ram_1_dout), .en(and_7_out), .clk(clk), .Q(byte_4), .clr(and_3_out));
  and and_7 (and_7_out, need_valC, decoder_1_out4);
  Register register_7 (.D(ram_1_dout), .en(and_8_out), .clk(clk), .Q(byte_5), .clr(and_3_out));
  and and_8 (and_8_out, need_valC, decoder_1_out5);
  Register register_8 (.D(ram_1_dout), .en(and_9_out), .clk(clk), .Q(byte_6), .clr(and_3_out));
  and and_9 (and_9_out, need_valC, decoder_1_out6);
  Register register_9 (.D(ram_1_dout), .en(and_10_out), .clk(clk), .Q(byte_7), .clr(and_3_out));
  and and_10 (and_10_out, need_valC, decoder_1_out7);
  Register register_10 (.D(ram_1_dout), .en(and_11_out), .clk(clk), .Q(byte_8), .clr(and_3_out));
  and and_11 (and_11_out, need_valC, decoder_1_out8);
  Register register_11 (.D(ram_1_dout), .en(and_12_out), .clk(clk), .Q(byte_9), .clr(and_3_out));
  and and_12 (and_12_out, need_valC, decoder_1_out9);
  Register #(.width(1)) register_12 (.D(1'b1), .en(and_4_out), .clk(clk), .Q(regs_loaded), .clr(and_2_out));
endmodule

module decode_and_write_back (
  input  Cnd,
  input  [3:0] icode,
  input  [3:0] rA,
  input  [3:0] rB,
  input  [63:0] valE,
  input  [63:0] valM,
  input  clk,
  input  in_8,
  output [63:0] valA,
  output [63:0] valB
);

  wire and_1_out, and_2_out, and_3_out, and_4_out, and_5_out, and_6_out, comparator_1_eq, comparator_2_eq,
       comparator_3_eq, comparator_4_eq, comparator_5_eq, comparator_6_eq, comparator_7_eq, comparator_8_eq,
       comparator_9_eq, comparator_10_eq, comparator_11_eq, comparator_12_eq, comparator_13_eq,
       comparator_14_eq, comparator_15_eq, comparator_17_eq, multiplexer_5_out, or_1_out, or_2_out, or_3_out,
       or_4_out, or_5_out, or_6_out, or_7_out, or_8_out;
  wire [3:0] counter_1_q, multiplexer_1_out, multiplexer_2_out, multiplexer_3_out, multiplexer_4_out,
       multiplexer_6_out, multiplexer_7_out, multiplexer_8_out;

  Comparator #(.width(4)) comparator_1 (.a(icode), .b(4'b0010), .eq(comparator_1_eq));  // open: gt, lt
  Comparator #(.width(4)) comparator_2 (.a(icode), .b(4'b0100), .eq(comparator_2_eq));  // open: gt, lt
  Comparator #(.width(4)) comparator_3 (.a(icode), .b(4'b0110), .eq(comparator_3_eq));  // open: gt, lt
  Comparator #(.width(4)) comparator_4 (.a(icode), .b(4'b1010), .eq(comparator_4_eq));  // open: gt, lt
  Comparator #(.width(4)) comparator_5 (.a(icode), .b(4'b1011), .eq(comparator_5_eq));  // open: gt, lt
  or or_1 (or_1_out, comparator_1_eq, comparator_2_eq, comparator_3_eq);
  and and_1 (and_1_out, or_1_out, in_8);
  or or_2 (or_2_out, comparator_4_eq, and_1_out);
  Multiplexer #(.width(4)) multiplexer_1 (.in0(4'b1111), .in1(rA), .out(multiplexer_1_out), .sel(or_2_out));
  Multiplexer #(.width(4)) multiplexer_2 (
    .in0(multiplexer_1_out), .in1(4'b0100), .out(multiplexer_2_out), .sel(comparator_5_eq));
  Comparator #(.width(4)) comparator_6 (.a(icode), .b(4'b0100), .eq(comparator_6_eq));  // open: gt, lt
  or or_3 (or_3_out, comparator_6_eq, comparator_7_eq, comparator_8_eq);
  Comparator #(.width(4)) comparator_7 (.a(icode), .b(4'b0101), .eq(comparator_7_eq));  // open: gt, lt
  Comparator #(.width(4)) comparator_8 (.a(icode), .b(4'b0110), .eq(comparator_8_eq));  // open: gt, lt
  Comparator #(.width(4)) comparator_9 (.a(icode), .b(4'b1011), .eq(comparator_9_eq));  // open: gt, lt
  or or_4 (or_4_out, comparator_4_eq, comparator_5_eq);
  and and_2 (and_2_out, or_3_out, in_8);
  or or_5 (or_5_out, comparator_9_eq, comparator_4_eq);
  Multiplexer #(.width(4)) multiplexer_3 (.in0(4'b1111), .in1(rB), .out(multiplexer_3_out), .sel(and_2_out));
  Multiplexer #(.width(4)) multiplexer_4 (
    .in0(multiplexer_3_out), .in1(4'b0100), .out(multiplexer_4_out), .sel(or_5_out));
  Comparator #(.width(4)) comparator_10 (.a(icode), .b(4'b0010), .eq(comparator_10_eq));  // open: gt, lt
  Comparator #(.width(4)) comparator_11 (.a(icode), .b(4'b0011), .eq(comparator_11_eq));  // open: gt, lt
  Comparator #(.width(4)) comparator_12 (.a(icode), .b(4'b0110), .eq(comparator_12_eq));  // open: gt, lt
  and and_3 (and_3_out, Cnd, comparator_10_eq);
  or or_6 (or_6_out, and_3_out, comparator_13_eq, comparator_11_eq, comparator_12_eq);
  Multiplexer multiplexer_5 (.in0(and_4_out), .in1(comparator_15_eq), .out(multiplexer_5_out), .sel(comparator_12_eq));
  Comparator #(.width(4)) comparator_13 (.a(icode), .b(4'b0101), .eq(comparator_13_eq));  // open: gt, lt
  Comparator #(.width(4)) comparator_14 (.a(icode), .b(4'b1011), .eq(comparator_14_eq));  // open: gt, lt
  and and_4 (and_4_out, or_6_out, comparator_15_eq);
  and and_5 (and_5_out, or_4_out, comparator_15_eq);
  Multiplexer #(.width(4)) multiplexer_6 (.in0(4'b1111), .in1(rB), .out(multiplexer_6_out), .sel(multiplexer_5_out));
  Multiplexer #(.width(4)) multiplexer_7 (
    .in0(multiplexer_6_out), .in1(4'b0100), .out(multiplexer_7_out), .sel(and_5_out));
  or or_7 (or_7_out, comparator_13_eq, comparator_14_eq);
  or or_8 (or_8_out, or_6_out, or_4_out);
  and and_6 (and_6_out, comparator_15_eq, or_7_out);
  Multiplexer #(.width(4)) multiplexer_8 (.in0(4'b1111), .in1(rA), .out(multiplexer_8_out), .sel(and_6_out));
  Counter #(.max('hf), .width(4)) counter_1 (
    .load(comparator_15_eq), .up(1'b1), .count(or_8_out), .clk(clk), .D(4'b0000), .Q(counter_1_q));  // open: clr, carry
  register_file register_file_1 (
    .srcB(multiplexer_4_out), .srcA(multiplexer_2_out), .valM(valM), .dstM(multiplexer_8_out), .valE(valE),
    .dstE(multiplexer_7_out), .clk(clk), .valB(valB), .valA(valA));
  Comparator #(.mode("unsigned"), .width(4)) comparator_15 (
    .a(counter_1_q), .b(4'b1110), .eq(comparator_15_eq));  // open: gt, lt
  Comparator #(.mode("unsigned"), .width(4)) comparator_16 (.a(counter_1_q), .b(4'b0001));  // open: gt, eq, lt
  Comparator #(.mode("unsigned"), .width(4)) comparator_17 (
    .a(counter_1_q), .b(4'b1000), .eq(comparator_17_eq));  // open: gt, lt
endmodule

module register_file (
  input  [63:0] valE,
  input  [3:0] srcA,
  input  [3:0] dstE,
  input  [63:0] valM,
  input  [3:0] srcB,
  input  [3:0] dstM,
  input  clk,
  output [63:0] valA,
  output [63:0] valB
);

  wire decoder_1_out0, decoder_1_out1, decoder_1_out2, decoder_1_out3, decoder_1_out4, decoder_1_out5,
       decoder_1_out6, decoder_1_out7, decoder_1_out8, decoder_1_out9, decoder_1_out10, decoder_1_out11,
       decoder_1_out12, decoder_1_out13, decoder_1_out14, decoder_2_out0, decoder_2_out1, decoder_2_out2,
       decoder_2_out3, decoder_2_out4, decoder_2_out5, decoder_2_out6, decoder_2_out7, decoder_2_out8,
       decoder_2_out9, decoder_2_out10, decoder_2_out11, decoder_2_out12, decoder_2_out13, decoder_2_out14,
       decoder_3_out0, decoder_3_out1, decoder_3_out2, decoder_3_out3, decoder_3_out4, decoder_3_out5,
       decoder_3_out6, decoder_3_out7, decoder_3_out8, decoder_3_out9, decoder_3_out10, decoder_3_out11,
       decoder_3_out12, decoder_3_out13, decoder_3_out14, decoder_4_out0, decoder_4_out1, decoder_4_out2,
       decoder_4_out3, decoder_4_out4, decoder_4_out5, decoder_4_out6, decoder_4_out7, decoder_4_out8,
       decoder_4_out9, decoder_4_out10, decoder_4_out11, decoder_4_out12, decoder_4_out13, decoder_4_out14,
       or_1_out, or_2_out, or_3_out, or_4_out, or_5_out, or_6_out, or_7_out, or_8_out, or_9_out, or_10_out,
       or_11_out, or_12_out, or_13_out, or_14_out, or_15_out;
  wire [63:0] multiplexer_1_out, multiplexer_2_out, multiplexer_3_out, multiplexer_4_out, multiplexer_5_out,
       multiplexer_6_out, multiplexer_7_out, multiplexer_8_out, multiplexer_9_out, multiplexer_10_out,
       multiplexer_11_out, multiplexer_12_out, multiplexer_13_out, multiplexer_14_out, multiplexer_15_out,
       r8_q, r9_q, r10_q, r11_q, r12_q, r13_q, r14_q, rax_q, rbp_q, rbx_q, rcx_q, rdi_q, rdx_q, rsi_q, rsp_q;

  Decoder #(.select(4)) decoder_1 (
    .out0(decoder_1_out0), .out1(decoder_1_out1), .out2(decoder_1_out2), .out3(decoder_1_out3),
    .out4(decoder_1_out4), .out5(decoder_1_out5), .out6(decoder_1_out6), .out7(decoder_1_out7),
    .out8(decoder_1_out8), .out9(decoder_1_out9), .out10(decoder_1_out10), .out11(decoder_1_out11),
    .out12(decoder_1_out12), .out13(decoder_1_out13), .out14(decoder_1_out14), .sel(dstE));  // open: out15, en
  Decoder #(.select(4)) decoder_2 (
    .out0(decoder_2_out0), .out1(decoder_2_out1), .out2(decoder_2_out2), .out3(decoder_2_out3),
    .out4(decoder_2_out4), .out5(decoder_2_out5), .out6(decoder_2_out6), .out7(decoder_2_out7),
    .out8(decoder_2_out8), .out9(decoder_2_out9), .out10(decoder_2_out10), .out11(decoder_2_out11),
    .out12(decoder_2_out12), .out13(decoder_2_out13), .out14(decoder_2_out14), .sel(dstM));  // open: out15, en
  Multiplexer #(.width(64)) multiplexer_1 (.in0(valE), .in1(valM), .out(multiplexer_1_out), .sel(decoder_2_out0));
  Multiplexer #(.width(64)) multiplexer_2 (.in0(valE), .in1(valM), .out(multiplexer_2_out), .sel(decoder_2_out1));
  Multiplexer #(.width(64)) multiplexer_3 (.in0(valE), .in1(valM), .out(multiplexer_3_out), .sel(decoder_2_out2));
  Multiplexer #(.width(64)) multiplexer_4 (.in0(valE), .in1(valM), .out(multiplexer_4_out), .sel(decoder_2_out3));
  Multiplexer #(.width(64)) multiplexer_5 (.in0(valE), .in1(valM), .out(multiplexer_5_out), .sel(decoder_2_out4));
  Multiplexer #(.width(64)) multiplexer_6 (.in0(valE), .in1(valM), .out(multiplexer_6_out), .sel(decoder_2_out5));
  Multiplexer #(.width(64)) multiplexer_7 (.in0(valE), .in1(valM), .out(multiplexer_7_out), .sel(decoder_2_out6));
  Multiplexer #(.width(64)) multiplexer_8 (.in0(valE), .in1(valM), .out(multiplexer_8_out), .sel(decoder_2_out7));
  Multiplexer #(.width(64)) multiplexer_9 (.in0(valE), .in1(valM), .out(multiplexer_9_out), .sel(decoder_2_out8));
  Multiplexer #(.width(64)) multiplexer_10 (.in0(valE), .in1(valM), .out(multiplexer_10_out), .sel(decoder_2_out9));
  Multiplexer #(.width(64)) multiplexer_11 (.in0(valE), .in1(valM), .out(multiplexer_11_out), .sel(decoder_2_out10));
  Multiplexer #(.width(64)) multiplexer_12 (.in0(valE), .in1(valM), .out(multiplexer_12_out), .sel(decoder_2_out11));
  Multiplexer #(.width(64)) multiplexer_13 (.in0(valE), .in1(valM), .out(multiplexer_13_out), .sel(decoder_2_out12));
  Multiplexer #(.width(64)) multiplexer_14 (.in0(valE), .in1(valM), .out(multiplexer_14_out), .sel(decoder_2_out13));
  Multiplexer #(.width(64)) multiplexer_15 (.in0(valE), .in1(valM), .out(multiplexer_15_out), .sel(decoder_2_out14));
  Register #(.width(64)) rax (.D(multiplexer_1_out), .en(or_1_out), .clk(clk), .Q(rax_q));  // open: clr
  or or_1 (or_1_out, decoder_1_out0, decoder_2_out0);
  Register #(.width(64)) rcx (.D(multiplexer_2_out), .en(or_2_out), .clk(clk), .Q(rcx_q));  // open: clr
  or or_2 (or_2_out, decoder_1_out1, decoder_2_out1);
  Register #(.width(64)) rdx (.D(multiplexer_3_out), .en(or_3_out), .clk(clk), .Q(rdx_q));  // open: clr
  or or_3 (or_3_out, decoder_1_out2, decoder_2_out2);
  Register #(.width(64)) rbx (.D(multiplexer_4_out), .en(or_4_out), .clk(clk), .Q(rbx_q));  // open: clr
  or or_4 (or_4_out, decoder_1_out3, decoder_2_out3);
  Register #(.width(64)) rsp (.D(multiplexer_5_out), .en(or_5_out), .clk(clk), .Q(rsp_q));  // open: clr
  or or_5 (or_5_out, decoder_1_out4, decoder_2_out4);
  Register #(.width(64)) rbp (.D(multiplexer_6_out), .en(or_6_out), .clk(clk), .Q(rbp_q));  // open: clr
  or or_6 (or_6_out, decoder_1_out5, decoder_2_out5);
  Register #(.width(64)) rsi (.D(multiplexer_7_out), .en(or_7_out), .clk(clk), .Q(rsi_q));  // open: clr
  or or_7 (or_7_out, decoder_1_out6, decoder_2_out6);
  Register #(.width(64)) rdi (.D(multiplexer_8_out), .en(or_8_out), .clk(clk), .Q(rdi_q));  // open: clr
  or or_8 (or_8_out, decoder_1_out7, decoder_2_out7);
  Register #(.width(64)) r8 (.D(multiplexer_9_out), .en(or_9_out), .clk(clk), .Q(r8_q));  // open: clr
  or or_9 (or_9_out, decoder_1_out8, decoder_2_out8);
  Register #(.width(64)) r9 (.D(multiplexer_10_out), .en(or_10_out), .clk(clk), .Q(r9_q));  // open: clr
  or or_10 (or_10_out, decoder_1_out9, decoder_2_out9);
  Register #(.width(64)) r10 (.D(multiplexer_11_out), .en(or_11_out), .clk(clk), .Q(r10_q));  // open: clr
  or or_11 (or_11_out, decoder_1_out10, decoder_2_out10);
  Register #(.width(64)) r11 (.D(multiplexer_12_out), .en(or_12_out), .clk(clk), .Q(r11_q));  // open: clr
  or or_12 (or_12_out, decoder_1_out11, decoder_2_out11);
  Register #(.width(64)) r12 (.D(multiplexer_13_out), .en(or_13_out), .clk(clk), .Q(r12_q));  // open: clr
  or or_13 (or_13_out, decoder_1_out12, decoder_2_out12);
  Register #(.width(64)) r13 (.D(multiplexer_14_out), .en(or_14_out), .clk(clk), .Q(r13_q));  // open: clr
  or or_14 (or_14_out, decoder_1_out13, decoder_2_out13);
  Register #(.width(64)) r14 (.D(multiplexer_15_out), .en(or_15_out), .clk(clk), .Q(r14_q));  // open: clr
  or or_15 (or_15_out, decoder_1_out14, decoder_2_out14);
  assign valA = decoder_3_out0 ? rax_q : 64'bz;  // Controlled_Buffer controlled_buffer_1
  assign valB = decoder_4_out0 ? rax_q : 64'bz;  // Controlled_Buffer controlled_buffer_2
  assign valA = decoder_3_out1 ? rcx_q : 64'bz;  // Controlled_Buffer controlled_buffer_3
  assign valB = decoder_4_out1 ? rcx_q : 64'bz;  // Controlled_Buffer controlled_buffer_4
  assign valA = decoder_3_out2 ? rdx_q : 64'bz;  // Controlled_Buffer controlled_buffer_5
  assign valB = decoder_4_out2 ? rdx_q : 64'bz;  // Controlled_Buffer controlled_buffer_6
  assign valA = decoder_3_out3 ? rbx_q : 64'bz;  // Controlled_Buffer controlled_buffer_7
  assign valB = decoder_4_out3 ? rbx_q : 64'bz;  // Controlled_Buffer controlled_buffer_8
  assign valA = decoder_3_out4 ? rsp_q : 64'bz;  // Controlled_Buffer controlled_buffer_9
  assign valB = decoder_4_out4 ? rsp_q : 64'bz;  // Controlled_Buffer controlled_buffer_10
  assign valA = decoder_3_out5 ? rbp_q : 64'bz;  // Controlled_Buffer controlled_buffer_11
  assign valB = decoder_4_out5 ? rbp_q : 64'bz;  // Controlled_Buffer controlled_buffer_12
  assign valA = decoder_3_out6 ? rsi_q : 64'bz;  // Controlled_Buffer controlled_buffer_13
  assign valB = decoder_4_out6 ? rsi_q : 64'bz;  // Controlled_Buffer controlled_buffer_14
  assign valA = decoder_3_out7 ? rdi_q : 64'bz;  // Controlled_Buffer controlled_buffer_15
  assign valB = decoder_4_out7 ? rdi_q : 64'bz;  // Controlled_Buffer controlled_buffer_16
  assign valA = decoder_3_out8 ? r8_q : 64'bz;  // Controlled_Buffer controlled_buffer_17
  assign valB = decoder_4_out8 ? r8_q : 64'bz;  // Controlled_Buffer controlled_buffer_18
  assign valA = decoder_3_out9 ? r9_q : 64'bz;  // Controlled_Buffer controlled_buffer_19
  assign valB = decoder_4_out9 ? r9_q : 64'bz;  // Controlled_Buffer controlled_buffer_20
  assign valA = decoder_3_out10 ? r10_q : 64'bz;  // Controlled_Buffer controlled_buffer_21
  assign valB = decoder_4_out10 ? r10_q : 64'bz;  // Controlled_Buffer controlled_buffer_22
  assign valA = decoder_3_out11 ? r11_q : 64'bz;  // Controlled_Buffer controlled_buffer_23
  assign valB = decoder_4_out11 ? r11_q : 64'bz;  // Controlled_Buffer controlled_buffer_24
  assign valA = decoder_3_out12 ? r12_q : 64'bz;  // Controlled_Buffer controlled_buffer_25
  assign valB = decoder_4_out12 ? r12_q : 64'bz;  // Controlled_Buffer controlled_buffer_26
  assign valA = decoder_3_out13 ? r13_q : 64'bz;  // Controlled_Buffer controlled_buffer_27
  assign valB = decoder_4_out13 ? r13_q : 64'bz;  // Controlled_Buffer controlled_buffer_28
  assign valA = decoder_3_out14 ? r14_q : 64'bz;  // Controlled_Buffer controlled_buffer_29
  assign valB = decoder_4_out14 ? r14_q : 64'bz;  // Controlled_Buffer controlled_buffer_30
  Decoder #(.select(4)) decoder_3 (
    .out0(decoder_3_out0), .out1(decoder_3_out1), .out2(decoder_3_out2), .out3(decoder_3_out3),
    .out4(decoder_3_out4), .out5(decoder_3_out5), .out6(decoder_3_out6), .out7(decoder_3_out7),
    .out8(decoder_3_out8), .out9(decoder_3_out9), .out10(decoder_3_out10), .out11(decoder_3_out11),
    .out12(decoder_3_out12), .out13(decoder_3_out13), .out14(decoder_3_out14), .sel(srcA));  // open: out15, en
  Decoder #(.select(4)) decoder_4 (
    .out0(decoder_4_out0), .out1(decoder_4_out1), .out2(decoder_4_out2), .out3(decoder_4_out3),
    .out4(decoder_4_out4), .out5(decoder_4_out5), .out6(decoder_4_out6), .out7(decoder_4_out7),
    .out8(decoder_4_out8), .out9(decoder_4_out9), .out10(decoder_4_out10), .out11(decoder_4_out11),
    .out12(decoder_4_out12), .out13(decoder_4_out13), .out14(decoder_4_out14), .sel(srcB));  // open: out15, en
endmodule

module memory (
  input  [3:0] icode,
  input  [63:0] valE,
  input  [63:0] valA,
  input  clk,
  output [63:0] vaM
);

  wire and_1_out, comparator_1_eq, comparator_2_eq, comparator_3_eq, comparator_4_eq, comparator_5_eq,
       or_1_out, or_2_out, or_3_out, or_4_out;
  wire [3:0] counter_1_q;
  wire [11:0] multiplexer_2_out, subtractor_1_out;
  wire [63:0] controlled_buffer_1_out, controlled_buffer_2_out, multiplexer_1_out;

  Counter #(.max('hf), .width(4)) counter_1 (
    .load(comparator_5_eq), .up(1'b1), .count(or_3_out), .clk(clk), .D(4'b0000), .Q(counter_1_q));  // open: clr, carry
  Comparator #(.width(4)) comparator_1 (.a(icode), .b(4'b0100), .eq(comparator_1_eq));  // open: gt, lt
  Comparator #(.width(4)) comparator_2 (.a(icode), .b(4'b1010), .eq(comparator_2_eq));  // open: gt, lt
  Comparator #(.width(4)) comparator_3 (.a(icode), .b(4'b0101), .eq(comparator_3_eq));  // open: gt, lt
  Comparator #(.width(4)) comparator_4 (.a(icode), .b(4'b1011), .eq(comparator_4_eq));  // open: gt, lt
  or or_1 (or_1_out, comparator_1_eq, comparator_3_eq, comparator_2_eq);
  or or_2 (or_2_out, comparator_2_eq, comparator_1_eq);
  assign controlled_buffer_1_out = or_1_out ? valE : 64'bz;  // Controlled_Buffer controlled_buffer_1
  Multiplexer #(.width(64)) multiplexer_1 (
    .in0(controlled_buffer_1_out), .in1(valA), .out(multiplexer_1_out), .sel(comparator_4_eq));
  or or_3 (or_3_out, comparator_1_eq, comparator_2_eq);
  or or_4 (or_4_out, comparator_3_eq, comparator_4_eq);
  assign controlled_buffer_2_out = or_2_out ? valA : 64'bz;  // Controlled_Buffer controlled_buffer_2
  Comparator #(.mode("unsigned"), .width(4)) comparator_5 (
    .a(counter_1_q), .b(4'b1110), .eq(comparator_5_eq));  // open: gt, lt
  Subtractor #(.width(12)) subtractor_1 (
    .a(multiplexer_1_out[11:0]), .b(12'h8), .out(subtractor_1_out));  // open: bin, bout
  and and_1 (and_1_out, or_3_out, comparator_5_eq);
  Multiplexer #(.width(12)) multiplexer_2 (
    .in0(multiplexer_1_out[11:0]), .in1(subtractor_1_out), .out(multiplexer_2_out), .sel(comparator_4_eq));
  RAM #(.addrWidth(12), .dataWidth(64)) ram_1 (
    .addr(multiplexer_2_out), .we(and_1_out), .oe(or_4_out), .clk(clk), .din(controlled_buffer_2_out),
    .dout(vaM));
endmodule
